# Fritzing sketch CocktailBar (saved by Fritzing 0.9.3b)
breadboards: 1

parts:
  Part1 = Arduino Uno (Rev3)
  HC-05_Bluetooth = Bluetooth HC-05 Macho
  Part2 = HX711 Weighing Sensor Module
  Load_Cell1 = Load Cell - Red/white/black/green
  S1 = H-Bridge with L298N
  M1 = DC Motor
  S2 = H-Bridge with L298N
  M3 = DC Motor
  M4 = DC Motor
  S3 = H-Bridge with L298N
  M5 = DC Motor
  M6 = DC Motor
  M2 = DC Motor
  J1 = Power Jack [package=power_jack_pth]
  J1_2 = Power Jack [package=power_jack_combo]

nets:
  N1: Part1.A0, Part2.DO/RX
  N2: Part1.A1, Part2.CK/TX
  N3: Part1.D8, S1.IN2
  N4: Part1.D9_PWM, S1.IN1
  N5: Part1.D10_PWM/SS, S3.IN4
  N6: Part1.D11_PWM/MOSI, S3.IN3
  N7: Part1.D12/MISO, S3.IN2
  N8: Part1.D13/SCK, S3.IN1
  GND: Part1.GND, HC-05_Bluetooth.GND, Part2.GND, S1.GND, S2.GND, S3.GND, J1.GND, J1_2.GND
  N9: Part1.D0/RX, HC-05_Bluetooth.TXD
  N10: Part1.D1/TX, HC-05_Bluetooth.RXD
  N11: Part1.D2, S2.IN4
  N12: Part1.D3_PWM, S2.IN3
  N13: Part1.D4, S2.IN2
  N14: Part1.D5_PWM, S2.IN1
  N15: Part1.D6_PWM, S1.IN4
  N16: Part1.D7, S1.IN3
  VCC: Part1.5V, HC-05_Bluetooth.VCC, Part2.VCC
  12V: Part1.VIN, S1.12V, S2.12V, S3.12V, J1.PWR, J1_2.PWR
  N17: Part2.E+, Load_Cell1.wire1
  N18: Part2.E-, Load_Cell1.wire3
  N19: Part2.A+, Load_Cell1.wire4
  N20: Part2.A-, Load_Cell1.wire2
  N21: S1.M1-01, M2.pin_2
  N22: S1.M1-02, M2.pin_1
  N23: S1.M2-01, M1.pin_2
  N24: S1.M2-02, M1.pin_1
  N25: S2.M1-01, M4.pin_2
  N26: S2.M1-02, M4.pin_1
  N27: S2.M2-01, M3.pin_2, S3.M1-02, M6.pin_1
  N28: S2.M2-02, M3.pin_1
  N29: S3.M1-01, M6.pin_2
  N30: S3.M2-01, M5.pin_2
  N31: S3.M2-02, M5.pin_1

custom parts:
  Load Cell - Red/white/black/green: A rectangle load cell/weighting pressure Sensor with four wires - Red, white, black, green. Normally corresponding with E+, E-, A+, A- respectively.
  H-Bridge with L298N: h-bridge
